# Fritzing sketch controller-schematic (saved by Fritzing 0.9.2b)
circuit board: 12.0363cm x 5.85386cm

parts:
  U1 = atmega328 [package=dip]
  Y1 = CRYSTAL [package=hc49us]
  C1 = Capacitor [package=cap-pth-small2]
  C2 = Capacitor [package=cap-pth-small2]
  Part1 = Thumb Joystick
  S1 = Momentary Switch [package=ksa_sealed_tac_switch]
  S2 = Momentary Switch [package=ksa_sealed_tac_switch]
  S3 = Momentary Switch [package=ksa_sealed_tac_switch]
  S4 = Momentary Switch [package=ksa_sealed_tac_switch]
  S5 = Momentary Switch [package=ksa_sealed_tac_switch]
  S6 = Momentary Switch [package=ksa_sealed_tac_switch]
  LED1 = LED - 5mm [color="Red (633nm)" package="5 mm [THT]"]
  LED2 = LED - 5mm [color="Blue (430nm)" package="5 mm [THT]"]
  R1 = Rotary Potentiometer (Large) [maximum_resistance=100kΩ package=THT]
  Part2 = FTDI Basic Programmer
  J1 = female pin header, 5 pins [form="♀ (female)"]
  X1 = USB Connectors [package=usb-microb]
  R8 = Resistor [tolerance=±10% resistance=1k package=THT]
  R7 = Resistor [tolerance=±5% resistance=1k package=THT]
  R9 = Resistor [tolerance=±5% resistance=1k package=THT]
  R6 = Resistor [tolerance=±5% resistance=1k package=THT]
  R5 = Resistor [tolerance=±5% resistance=1k package=THT]
  R3 = Resistor [tolerance=±5% resistance=1k package=THT]
  R2 = Resistor [tolerance=±5% resistance=1k package=THT]
  R4 = Resistor [tolerance=±5% resistance=1k package=THT]

nets:
  N1: U1.D0_(RX), Part2.RXI
  N2: U1.D1_(TX), Part2.TXO
  N3: U1.D2, S1.2, R4.Pin_0
  N4: U1.D3_(PWM), R2.Pin_1
  N5: U1.D4, Part1.SEL
  VCC: U1.VCC, U1.AVCC, Part1.VCC, R1.leg2, Part2.POWER, J1.pin2, X1.VBUS, R8.Pin_0, R7.Pin_0, R9.Pin_0, R6.Pin_0, R5.Pin_0, R4.Pin_1
  GND: U1.GND, Part1.GND, S1.4, S2.3, S3.4, S4.4, S5.4, S6.4, LED1.cathode, LED2.cathode, R1.leg1, Part2.GND, J1.pin3, X1.GND
  N6: U1.XLAT1, Y1.2, C1.2
  N7: U1.XLAT2, Y1.1, C2.1
  N8: U1.D5_(PWM), R3.Pin_1
  N9: U1.D6_(PWM), S6.2, R5.Pin_1
  N10: U1.D7, S5.2, R6.Pin_1
  N11: U1.D8, S3.2, R9.Pin_1
  N12: U1.D9_(PWM), S4.2, R7.Pin_1
  N13: U1.D10_(PWM), S2.1, R8.Pin_1
  N14: U1.D13, J1.pin1
  N15: U1.A0, R1.wiper
  N16: U1.A1, Part1.VERT
  N17: U1.A2, Part1.HORZ
  N18: C1.1, C2.2
  N19: LED1.anode, R2.Pin_0
  N20: LED2.anode, R3.Pin_0
